# Fritzing sketch sketch (saved by Fritzing 0.9.3b)

parts:
  Part1 = Arduino Mega ADK (Rev3)
  Part2 = Arduino Prototyping Shield
  U1 = Mini-360 DC-DC Buck converter [package=THT]
  U2 = NEO 6M GPS
  U5 = RS232 Transceiver [package=so016]
  DIN2 = DIN-5 jack (MIDI) [package=THT]
  Adafruit_HUZZAH_ESP8266_Breakout1 = Adafruit HUZZAH ESP8266 Breakout [part_number=2471]
  U6 = RS232 Transceiver [package=so016]
  Part3 = MicroSD Card Module

nets:
  N1: Part1.D19/RX1, Adafruit_HUZZAH_ESP8266_Breakout1.RX
  N2: Part1.D18/TX1, Adafruit_HUZZAH_ESP8266_Breakout1.TX
  N3: Part1.D17/RX2, U2.RXD
  N4: Part1.D16/TX2, U2.TXD
  N5: Part1.D46, U5.R2IN
  N6: Part1.D47, U5.T2OUT
  N7: Part2.D12, Part3.MISO
  VCC: Part2.+5V, U2.VCC, U5.V+, Adafruit_HUZZAH_ESP8266_Breakout1.V+, U6.VCC, Part3.VCC
  N8: Part2.D13, Part3.SCK
  N9: Part2.D11, Part3.MOSI
  GND: Part2.GND, U1.OUT-, U2.GND, U5.V-, Adafruit_HUZZAH_ESP8266_Breakout1.GND, U6.GND, Part3.GND
  N10: Part2.D4, Part3.CS
  N11: Part2.+9V, U1.OUT+
  N12: U5.R1OUT, DIN2.4
  N13: U5.T1OUT, DIN2.5

custom parts:
  Mini-360 DC-DC Buck converter: Mini-360 DC-DC Buck converter. Tiny buck step down voltage converter, input voltage 4.75 to 23V output 1 to 17V adjustable. Available from ebay and the like.
  NEO 6M GPS: uSD module
